# Fritzing sketch HandsOnArduinoShema (saved by Fritzing 0.9.4)
breadboards: 1

parts:
  Keypad4x1 = Keypad Membran 4x4
  Part1 = Arduino Uno (Rev3)
  J1 = Piezo Speaker
  R1 = Resistor [tolerance=±5% resistance=10k package="0402 [SMD]"]
  R3 = Resistor [tolerance=±5% resistance=3.3k package="0402 [SMD]"]
  R4 = Resistor [tolerance=±5% resistance=2.2 package="0402 [SMD]"]
  R5 = Resistor [tolerance=±5% resistance=1k package="0402 [SMD]"]
  R6 = Resistor [tolerance=±5% resistance=330 package="0402 [SMD]"]
  R7 = Resistor [tolerance=±5% resistance=220 package="0402 [SMD]"]
  R8 = Resistor [tolerance=±5% resistance=100 package="0402 [SMD]"]
  R9 = Resistor [tolerance=±5% resistance=10 package="0402 [SMD]"]
  R10 = Resistor [tolerance=±5% resistance=10k package="0402 [SMD]"]

nets:
  N1: Keypad4x1.Pin1, R9.Pin_0
  N2: Keypad4x1.Pin2, R8.Pin_0
  N3: Keypad4x1.Pin3, R7.Pin_0
  N4: Keypad4x1.Pin4, R6.Pin_0
  N5: Keypad4x1.Pin5, R5.Pin_0
  N6: Keypad4x1.Pin6, R4.Pin_0
  N7: Keypad4x1.Pin7, R3.Pin_0
  N8: Keypad4x1.Pin8, R1.Pin_0
  N9: Part1.A0, J1.pin2
  N10: Part1.A1, R1.Pin_1, R3.Pin_1, R4.Pin_1, R5.Pin_1, R10.Pin_0
  N11: Part1.5V, R10.Pin_1
  N12: Part1.GND, J1.pin1, R6.Pin_1, R7.Pin_1, R8.Pin_1, R9.Pin_1

custom parts:
  Keypad Membran 4x4: Membrane Keypad 4x4 Matrix
